# Fritzing sketch ULTRASONIC_LED_SENSOR_METER (saved by Fritzing 0.9.1b)
breadboards: 1

parts:
  Onderdeel1 = Arduino Uno (Rev3)
  Onderdeel2 = SRF05 Ultrasonic Rangefinder
  R1 = Resistor [tolerance=±1% resistance=68 package=THT]
  R2 = Resistor [tolerance=±1% resistance=68 package=THT]
  R3 = Resistor [tolerance=±1% resistance=68 package=THT]
  R4 = Resistor [tolerance=±1% resistance=68 package=THT]
  R5 = Resistor [tolerance=±1% resistance=68 package=THT]
  LED1 = LED - 5mm [color="Red (633nm)" package="5 mm [THT]"]
  LED2 = LED - 5mm [color="Red (633nm)" package="5 mm [THT]"]
  LED3 = LED - 5mm [color="Red (633nm)" package="5 mm [THT]"]
  LED4 = LED - 5mm [color="Red (633nm)" package="5 mm [THT]"]
  LED5 = LED - 5mm [color="Red (633nm)" package="5 mm [THT]"]

nets:
  N1: Onderdeel1.D8, LED3.cathode
  N2: Onderdeel1.D9_PWM, LED2.cathode
  N3: Onderdeel1.D10_PWM/SS, LED1.cathode
  N4: Onderdeel1.D12/MISO, Onderdeel2.Echo
  N5: Onderdeel1.D13/SCK, Onderdeel2.Trig
  N6: Onderdeel1.D6_PWM, LED5.cathode
  N7: Onderdeel1.D7, LED4.cathode
  5V: Onderdeel1.5V, Onderdeel2.VCC, R1.Pin_1, R2.Pin_1, R3.Pin_1, R4.Pin_1, R5.Pin_1
  GND: Onderdeel1.GND, Onderdeel2.GND
  N8: R1.Pin_0, LED2.anode
  N9: R2.Pin_0, LED3.anode
  N10: R3.Pin_0, LED1.anode
  N11: R4.Pin_0, LED4.anode
  N12: R5.Pin_0, LED5.anode

// code stored in the sketch: Ultrasonic sensor with leds.ino
#define trigPin 13
#define echoPin 12
#define led 6
#define led2 7
#define led3 8
#define led4 9
#define led5 10


void setup() {
    Serial.begin (9600);
    pinMode(trigPin, OUTPUT);
    pinMode(echoPin, INPUT);
    pinMode(led, OUTPUT);
    pinMode(led2, OUTPUT);
    pinMode(led3, OUTPUT);
    pinMode(led4, OUTPUT);
    pinMode(led5, OUTPUT);
    
}

void loop() {
    long duration, distance;
    digitalWrite(trigPin, LOW);
    delayMicroseconds(2);
    digitalWrite(trigPin, HIGH);
    
    delayMicroseconds(10);
    digitalWrite(trigPin, LOW);
    duration = pulseIn(echoPin, HIGH);
    distance = (duration/2) / 29.1;
    if (distance < 10) {
        digitalWrite(led,LOW);
        digitalWrite(led2,LOW);
        digitalWrite(led3,LOW);
        digitalWrite(led4,LOW);
        digitalWrite(led5,LOW);
        } else if (distance >= 10 && distance < 20){
        digitalWrite(led,LOW);
        digitalWrite(led2,LOW);
        digitalWrite(led3,LOW);
        digitalWrite(led4,LOW);
        digitalWrite(led5,HIGH);
        } else if (distance >= 20 && distance < 30){
        digitalWrite(led,LOW);
        digitalWrite(led2,LOW);
        digitalWrite(led3,LOW);
        digitalWrite(led4,HIGH);
        digitalWrite(led5,HIGH);
        } else if (distance >= 30 && distance < 40){
        digitalWrite(led,LOW);
        digitalWrite(led2,LOW);
        digitalWrite(led3,HIGH);
        digitalWrite(led4,HIGH);
        digitalWrite(led5,HIGH);
        } else if (distance >= 40 && distance <= 50){
        digitalWrite(led,LOW);
        digitalWrite(led2,HIGH);
        digitalWrite(led3,HIGH);
        digitalWrite(led4,HIGH);
        digitalWrite(led5,HIGH);
        } else {
        digitalWrite(led,HIGH);
        digitalWrite(led2,HIGH);
        digitalWrite(led3,HIGH);
        digitalWrite(led4,HIGH);
        digitalWrite(led5,HIGH);
    }
    if (distance >= 200 || distance <= 0){
        Serial.println("Out of range");
    }
    else {
        Serial.print(distance);
        Serial.println(" cm");
    }
    delay(50);
}
