# Fritzing sketch DHT22 (saved by Fritzing 0.9.1b)
circuit board: 8.46667cm x 5.64444cm
breadboards: 1

parts:
  Arduino_UNO = Arduino Uno (Rev3)
  R1 = Resistor [tolerance=±5% resistance=10k package=THT]
  DHT1 = DHT22 Humidity and Temperature Sensor

nets:
  N1: Arduino_UNO.D2, R1.Pin_1, DHT1.DATA
  5V: Arduino_UNO.5V, R1.Pin_0, DHT1.VDD
  GND: Arduino_UNO.GND, DHT1.GND
