# Fritzing sketch PHOTORESISTOR (saved by Fritzing 0.9.1b)
circuit board: 8.46667cm x 5.64444cm
breadboards: 1

parts:
  Arduino_UNO = Arduino Uno (Rev3)
  R1 = PHOTOCELL [package=photocell-kit]
  R2 = Resistor [tolerance=±5% resistance=10k package=THT]

nets:
  N1: Arduino_UNO.A0, R1.P$1, R2.Pin_0
  N2: Arduino_UNO.GND, R2.Pin_1
  N3: Arduino_UNO.5V, R1.P$2
