# Fritzing sketch WIFIESP8266 (saved by Fritzing 0.9.1b)
circuit board: 8.46667cm x 5.64444cm
breadboards: 1

parts:
  Arduino_UNO = Arduino Uno (Rev3)
  U1 = ESP8266 WiFi Module [part_number=ESP8266]

nets:
  GND: Arduino_UNO.GND, U1.GND
  N1: Arduino_UNO.D0/RX, U1.RXD
  N2: Arduino_UNO.D1/TX, U1.TXD
  3V3: Arduino_UNO.3V3, U1.VCC, U1.CH_PD

custom parts:
  ESP8266 WiFi Module: Generic WiFi Module based on the ESP8266 with onboard PCB antenna and UART communications
